// Logisim project ej2.circ as structural Verilog: 1 circuit, main circuit main
module main (
  input  [3:0] in_1,
  input  [3:0] in_2,
  input  in_3,
  output [3:0] out_4
);

  wire [3:0] xor_1_out;

  Hex_Digit_Display hex_digit_display_1 (.value(in_1));  // open: dp
  Hex_Digit_Display hex_digit_display_2 (.value(in_2));  // open: dp
  assign xor_1_out = in_2 ^ {4{in_3}};  // XOR_Gate xor_1, 4 bits wide
  Hex_Digit_Display hex_digit_display_3 (.value(out_4));  // open: dp
  Adder #(.width(4)) adder_1 (.a(in_1), .b(xor_1_out), .out(out_4), .cin(in_3));  // open: cout

  // Notes on the sheet:
  //   Seleccionador de Suma o Resta 
  //   0 para la suma 1 para la resta
endmodule
