// Logisim project ej3.circ as structural Verilog: 2 circuits, main circuit main
module main (
  input  [1:0] b,
  input  [3:0] a,
  output [5:0] out_3
);

  wire [3:0] and_8_out;
  wire [4:1] and_4_out;

  and and_1 (and_4_out[4], b[1], a[3]);
  and and_2 (and_4_out[3], b[1], a[2]);
  and and_3 (and_4_out[2], b[1], a[1]);
  and and_4 (and_4_out[1], b[1], a[0]);
  and and_5 (and_8_out[3], b[0], a[3]);
  and and_6 (and_8_out[2], b[0], a[2]);
  and and_7 (and_8_out[1], b[0], a[1]);
  and and_8 (and_8_out[0], b[0], a[0]);
  sumador_de_5 sumador_de_5_1 (.in_1({1'b0, and_8_out}), .in_2({and_4_out, 1'b0}), .out_3(out_3));

  // Notes on the sheet:
  //   SUMADOR BCD
endmodule

module sumador_de_5 (
  input  [4:0] in_1,
  input  [4:0] in_2,
  output [5:0] out_3
);

  wire adder_1_cout;
  wire [3:2] adder_2_out;

  Adder #(.width(4)) adder_1 (.a(in_1[3:0]), .b(in_2[3:0]), .out(out_3[3:0]), .cout(adder_1_cout));  // open: cin
  Adder #(.width(4)) adder_2 (
    .a({3'b000, in_1[4]}), .b({3'b000, in_2[4]}), .out({adder_2_out, out_3[5:4]}), .cin(adder_1_cout));  // open: cout
endmodule
