// Logisim project ej5.circ as structural Verilog: 1 circuit, main circuit main
module main (
  input  e,
  input  a,
  input  b,
  input  c,
  input  d
);

  wire multiplexer_1_out;

  Multiplexer #(.select(4)) multiplexer_1 (
    .in0(1'b0), .in1(e), .in2(1'b0), .in3(e), .in4(1'b0), .in5(e), .in6(1'b0), .in7(e), .in8(1'b0),
    .in9(1'b1), .in10(e), .in11(1'b1), .in12(e), .in13(1'b1), .in14(e), .in15(1'b1), .out(multiplexer_1_out),
    .sel({a, b, c, d}));  // open: en
  LED led_1 (.in(multiplexer_1_out));
endmodule
