// Logisim project ej6.circ as structural Verilog: 3 circuits, main circuit main
module main (
  input  [1:0] A,
  input  [1:0] B,
  input  [1:0] g,
  output [1:0] out_4
);

  wire [1:0] Media_por_defecto_out_3, Media_por_exceso_out_3;

  Hex_Digit_Display hex_digit_display_1 (.value({2'b00, A}));  // open: dp
  medias_por_defecto Media_por_defecto (.A(A), .B(B), .out_3(Media_por_defecto_out_3));
  medias_por_exceso Media_por_exceso (.A(A), .B(B), .out_3(Media_por_exceso_out_3));
  Hex_Digit_Display hex_digit_display_2 (.value({2'b00, B}));  // open: dp
  Multiplexer #(.select(2), .width(2)) multiplexer_1 (
    .in0(Media_por_defecto_out_3), .in1(A), .in2(B), .in3(Media_por_exceso_out_3), .out(out_4), .sel(g),
    .en(1'b1));
  Hex_Digit_Display hex_digit_display_3 (.value({2'b00, out_4}));  // open: dp
endmodule

module medias_por_defecto (
  input  [1:0] A,
  input  [1:0] B,
  output [1:0] out_3
);

  wire and_1_out, and_2_out, and_3_out, and_4_out, and_5_out, and_6_out, and_7_out, and_8_out, and_9_out,
       not_1_out, not_2_out, not_3_out, not_4_out, not_5_out, not_6_out, not_7_out, not_8_out, not_9_out,
       not_10_out;

  and and_1 (and_1_out, A[0], B[1], B[0]);
  and and_2 (and_2_out, A[1], B[1]);
  and and_3 (and_3_out, A[1], A[0], B[0]);
  not not_1 (not_1_out, A[1]);
  not not_2 (not_2_out, A[0]);
  not not_3 (not_3_out, A[1]);
  not not_4 (not_4_out, B[0]);
  not not_5 (not_5_out, A[1]);
  not not_6 (not_6_out, B[1]);
  not not_7 (not_7_out, A[0]);
  not not_8 (not_8_out, B[1]);
  not not_9 (not_9_out, B[1]);
  not not_10 (not_10_out, B[0]);
  or or_1 (out_3[1], and_1_out, and_2_out, and_3_out);
  and and_4 (and_4_out, not_1_out, not_2_out, B[1]);
  and and_5 (and_5_out, not_3_out, B[1], not_4_out);
  and and_6 (and_6_out, not_5_out, A[0], not_6_out, B[0]);
  and and_7 (and_7_out, A[1], not_7_out, not_8_out);
  and and_8 (and_8_out, A[1], not_9_out, not_10_out);
  and and_9 (and_9_out, A[1], A[0], B[1], B[0]);
  or or_2 (out_3[0], and_4_out, and_5_out, and_6_out, and_7_out, and_8_out, and_9_out);
endmodule

module medias_por_exceso (
  input  [1:0] A,
  input  [1:0] B,
  output [1:0] out_3
);

  wire and_1_out, and_2_out, and_3_out, and_4_out, and_5_out, and_6_out, and_7_out, and_8_out, and_9_out,
       and_10_out, and_11_out, not_1_out, not_2_out, not_3_out, not_4_out, not_5_out, not_6_out, not_7_out,
       not_8_out, not_9_out, not_10_out;

  and and_1 (and_1_out, B[1], B[0]);
  and and_2 (and_2_out, A[0], B[1]);
  and and_3 (and_3_out, A[1], B[0]);
  and and_4 (and_4_out, A[1], B[1]);
  and and_5 (and_5_out, A[1], A[0]);
  not not_1 (not_1_out, A[1]);
  not not_2 (not_2_out, B[1]);
  not not_3 (not_3_out, A[1]);
  not not_4 (not_4_out, A[0]);
  not not_5 (not_5_out, B[0]);
  not not_6 (not_6_out, A[1]);
  not not_7 (not_7_out, B[1]);
  not not_8 (not_8_out, A[0]);
  not not_9 (not_9_out, B[1]);
  not not_10 (not_10_out, B[0]);
  or or_1 (out_3[1], and_1_out, and_2_out, and_3_out, and_4_out, and_5_out);
  and and_6 (and_6_out, not_1_out, not_2_out, B[0]);
  and and_7 (and_7_out, not_3_out, not_4_out, B[1], not_5_out);
  and and_8 (and_8_out, not_6_out, A[0], not_7_out);
  and and_9 (and_9_out, A[1], not_8_out, not_9_out, not_10_out);
  and and_10 (and_10_out, A[1], B[1], B[0]);
  and and_11 (and_11_out, A[1], A[0], B[1]);
  or or_2 (out_3[0], and_6_out, and_7_out, and_8_out, and_9_out, and_10_out, and_11_out);
endmodule
