// Logisim project Ej1.circ as structural Verilog: 1 circuit, main circuit main
module main (
  input  R,
  input  S,
  output Q,
  output nQ
);

  wire clock_1_out, nand_1_out, nand_2_out;

  Clock clock_1 (.out(clock_1_out));
  nand nand_1 (nand_1_out, R, clock_1_out);
  nand nand_2 (nand_2_out, clock_1_out, S);
  nand nand_3 (Q, nand_2_out, nQ);
  nand nand_4 (nQ, Q, nand_1_out);

  // Notes on the sheet:
  //   K
endmodule
