// Logisim project Ej2.circ as structural Verilog: 1 circuit, main circuit main
module main (
  input  C,
  input  S,
  input  R,
  input  P,
  output out_5,
  output out_6
);

  wire clock_1_out, nand_1_out, nand_2_out, nand_3_out, nand_4_out, nand_5_out, nand_6_out, nand_7_out,
       nand_8_out;

  Clock clock_1 (.out(clock_1_out));
  nand nand_1 (nand_1_out, S, clock_1_out);
  nand nand_2 (nand_2_out, clock_1_out, R);
  nand nand_3 (nand_3_out, nand_2_out, nand_8_out);
  nand nand_4 (nand_4_out, nand_7_out, nand_1_out);
  nand nand_5 (nand_5_out, C, nand_3_out);
  nand nand_6 (nand_6_out, nand_4_out, P);
  nand nand_7 (nand_7_out, nand_5_out, nand_5_out);
  nand nand_8 (nand_8_out, nand_6_out, nand_6_out);
  nand nand_9 (out_5, nand_5_out, nand_5_out);
  nand nand_10 (out_6, nand_6_out, nand_6_out);

  // Notes on the sheet:
  //   K
  //   Q
  //   /Q
endmodule
