// Logisim project ej3.circ as structural Verilog: 1 circuit, main circuit main
module main (
  input  J,
  input  K,
  input  PRESET,
  input  CLEAR,
  output q,
  output q_prime
);

  wire clock_1_out;

  Clock clock_1 (.out(clock_1_out));
  J_K_Flip_Flop j_k_ff_1 (
    .J(J), .clk(clock_1_out), .K(K), .Q(q), .Qn(q_prime), .preset(PRESET), .en(1'b1), .reset(CLEAR));

  // Notes on the sheet:
  //   CLK
endmodule
