// Logisim project ej4.circ as structural Verilog: 1 circuit, main circuit main
module main (
  input  in_1,
  input  in_2,
  input  Selector
);

  wire and_1_out, and_2_out, clock_1_out;
  wire [3:0] j_k_ff_1_q;

  Clock clock_1 (.out(clock_1_out));
  // Probe on j_k_ff_1_q[0]
  J_K_Flip_Flop #(.trigger("falling")) j_k_ff_1 (
    .J(in_1), .clk(clock_1_out), .K(in_1), .Q(j_k_ff_1_q[0]), .preset(in_2), .reset(and_1_out));  // open: Qn, en
  J_K_Flip_Flop #(.trigger("falling")) j_k_ff_2 (
    .J(in_1), .clk(j_k_ff_1_q[0]), .K(in_1), .Q(j_k_ff_1_q[1]), .preset(in_2), .reset(and_2_out));  // open: Qn, en
  and and_1 (and_1_out, j_k_ff_1_q[2], j_k_ff_1_q[3], Selector);
  and and_2 (and_2_out, and_1_out, j_k_ff_1_q[2], 1'b0);
  J_K_Flip_Flop #(.trigger("falling")) j_k_ff_3 (
    .J(in_1), .clk(j_k_ff_1_q[1]), .K(in_1), .Q(j_k_ff_1_q[2]), .preset(in_2), .reset(and_2_out));  // open: Qn, en
  J_K_Flip_Flop #(.trigger("falling")) j_k_ff_4 (
    .J(in_1), .clk(j_k_ff_1_q[2]), .K(in_1), .Q(j_k_ff_1_q[3]), .preset(in_2), .reset(and_2_out));  // open: Qn, en
  Hex_Digit_Display hex_digit_display_1 (.value(j_k_ff_1_q));  // open: dp
endmodule
