// Logisim project ej5.circ as structural Verilog: 3 circuits, main circuit main
module main (
  input  [1:0] m,
  input  clk,
  output p,
  output d
);

  wire combinacion_1_d, combinacion_1_j0, combinacion_1_j1, combinacion_1_k0, combinacion_1_k1,
       combinacion_1_p, memo_1_out_6, memo_1_out_7;

  combinacion combinacion_1 (
    .m1(m[1]), .m0(m[0]), .q1(memo_1_out_6), .q0(memo_1_out_7), .p(combinacion_1_p), .d(combinacion_1_d),
    .J1(combinacion_1_j1), .K1(combinacion_1_k1), .J0(combinacion_1_j0), .K0(combinacion_1_k0));
  memo memo_1 (
    .clk(clk), .J1(combinacion_1_j1), .K1(combinacion_1_k1), .j0(combinacion_1_j0), .k0(combinacion_1_k0),
    .out_6(memo_1_out_6), .out_7(memo_1_out_7));
  D_Flip_Flop d_ff_1 (.clk(clk), .D(combinacion_1_p), .Q(p));  // open: Qn, preset, en, reset
  D_Flip_Flop d_ff_2 (.clk(clk), .D(combinacion_1_d), .Q(d));  // open: Qn, preset, en, reset
endmodule

module combinacion (
  input  m1,
  input  m0,
  input  q1,
  input  q0,
  output p,
  output d,
  output J1,
  output K1,
  output J0,
  output K0
);

  wire and_1_out, and_2_out, and_5_out, and_6_out, not_1_out, not_2_out, not_3_out, not_4_out;

  not not_1 (not_1_out, m1);
  not not_2 (not_2_out, q1);
  not not_3 (not_3_out, m1);
  not not_4 (not_4_out, q0);
  and and_1 (and_1_out, m0, q1);
  and and_2 (and_2_out, m1, q0);
  and and_3 (d, m1, q1);
  and and_4 (J0, not_1_out, m0, not_2_out);
  or or_1 (p, and_1_out, and_2_out);
  and and_5 (and_5_out, not_3_out, q0, m0);
  and and_6 (and_6_out, m1, not_4_out);
  or or_2 (J1, and_5_out, and_6_out);

  assign K0 = m0;
  assign K1 = m0;
endmodule

module memo (
  input  clk,
  input  J1,
  input  K1,
  input  j0,
  input  k0,
  output out_6,
  output out_7
);

  J_K_Flip_Flop j_k_ff_1 (.J(J1), .clk(clk), .K(K1), .Q(out_6));  // open: Qn, preset, en, reset
  J_K_Flip_Flop j_k_ff_2 (.J(j0), .clk(clk), .K(k0), .Q(out_7));  // open: Qn, preset, en, reset
endmodule
