// Logisim project ej1.circ as structural Verilog: 2 circuits, main circuit main
module main (
  input  [3:0] a,
  input  [3:0] b,
  output [3:0] out_3,
  output [3:0] out_4
);

  wire adder_1_cout;
  wire [3:0] adder_1_out;

  Adder #(.width(4)) adder_1 (.a(a), .b(b), .out(adder_1_out), .cout(adder_1_cout));  // open: cin
  control_de_acarreos control_de_acarreos_1 (
    .c(adder_1_cout), .s3(adder_1_out[3]), .s2(adder_1_out[2]), .s1(adder_1_out[1]), .s0(adder_1_out[0]),
    .cout(out_3[0]));
  Hex_Digit_Display hex_digit_display_1 (.value({3'b000, out_3[0]}));  // open: dp
  Adder #(.width(4)) adder_2 (.a(adder_1_out), .b({1'b0, {2{out_3[0]}}, 1'b0}), .out(out_4));  // open: cin, cout
  Hex_Digit_Display hex_digit_display_2 (.value(out_4));  // open: dp

  assign out_3[3:1] = 3'b000;
endmodule

module control_de_acarreos (
  input  c,
  input  s3,
  input  s2,
  input  s1,
  input  s0,
  output cout
);

  wire and_1_out, and_2_out;

  and and_1 (and_1_out, s3, s1);
  and and_2 (and_2_out, s3, c);
  or or_1 (cout, and_1_out, and_2_out);
endmodule
