// Logisim project ej2.circ as structural Verilog: 2 circuits, main circuit main
module main (
  output [3:0] A,
  output [3:0] B,
  output hat,
  output [3:0] out_4,
  output hat_2,
  output hat_3
);

  wire clock_1_out, clock_2_out, clock_3_out, counter_3_q;

  Clock clock_1 (.out(clock_1_out));
  Clock clock_2 (.out(clock_2_out));
  Counter #(.width(4), .max('hf)) counter_1 (.Q(A), .carry(hat), .clk(clock_1_out));  // open: load, D, count, clr
  Counter #(.width(4), .max('hf)) counter_2 (.Q(B), .carry(hat_2), .clk(clock_2_out));  // open: load, D, count, clr
  Clock clock_3 (.out(clock_3_out));
  Counter #(.width(1), .max('h1)) counter_3 (
    .Q(counter_3_q), .carry(hat_3), .clk(clock_3_out));  // open: load, D, count, clr
  sumador sumador_1 (.A(A), .B(B), .s_r(counter_3_q), .R(out_4));
endmodule

module sumador (
  input  [3:0] A,
  input  [3:0] B,
  input  s_r,
  output [3:0] R
);

  wire [3:0] xor_1_out;

  assign xor_1_out = B ^ {4{s_r}};  // XOR_Gate xor_1, 4 bits wide
  Adder #(.width(4)) adder_1 (.a(A), .b(xor_1_out), .out(R), .cin(s_r));  // open: cout
endmodule
