// Logisim project ej3.circ as structural Verilog: 3 circuits, main circuit main
module main (
  output [1:0] A,
  output [3:0] B,
  output [5:0] out_3,
  output hat,
  output hat_2
);

  wire clock_1_out, clock_2_out;

  Counter #(.width(2), .max('h3)) counter_1 (.Q(A), .carry(hat), .clk(clock_1_out));  // open: load, D, count, clr
  Clock clock_1 (.out(clock_1_out));
  Clock clock_2 (.out(clock_2_out));
  Counter #(.width(4), .max('hf)) counter_2 (.Q(B), .carry(hat_2), .clk(clock_2_out));  // open: load, D, count, clr
  ej3 ej3_1 (.b(A), .a(B), .out_3(out_3));
endmodule

module ej3 (
  input  [1:0] b,
  input  [3:0] a,
  output [5:0] out_3
);

  wire [3:0] and_4_out;
  wire [4:1] and_8_out;

  and and_1 (and_4_out[3], b[0], a[3]);
  and and_2 (and_4_out[2], b[0], a[2]);
  and and_3 (and_4_out[1], b[0], a[1]);
  and and_4 (and_4_out[0], b[0], a[0]);
  and and_5 (and_8_out[4], b[1], a[3]);
  and and_6 (and_8_out[3], b[1], a[2]);
  and and_7 (and_8_out[2], b[1], a[1]);
  and and_8 (and_8_out[1], b[1], a[0]);
  sum5 sum5 (.x({1'b0, and_4_out}), .y({and_8_out, 1'b0}), .out_3(out_3));
endmodule

module sum5 (
  input  [4:0] x,
  input  [4:0] y,
  output [5:0] out_3
);

  wire adder_1_cout;
  wire [3:2] adder_2_out;

  Adder #(.width(4)) adder_1 (.a(x[3:0]), .b(y[3:0]), .out(out_3[3:0]), .cout(adder_1_cout));  // open: cin
  Adder #(.width(4)) adder_2 (
    .a({3'b000, x[4]}), .b({3'b000, y[4]}), .out({adder_2_out, out_3[5:4]}), .cin(adder_1_cout));  // open: cout
endmodule
