// Logisim project ej4.circ as structural Verilog: 3 circuits, main circuit main
module main (
  input  enable,
  output out_2,
  output hat
);

  wire clock_1_out;
  wire [3:0] counter_1_q;

  Clock clock_1 (.out(clock_1_out));
  Counter #(.width(4), .max('hf)) counter_1 (
    .Q(counter_1_q), .carry(hat), .clk(clock_1_out));  // open: load, D, count, clr
  ej4_primo ej4_primo_1 (.enable(enable), .in_2(counter_1_q), .out_3(out_2));
endmodule

module ej4_trampa (
  input  n3,
  input  n2,
  input  n1,
  input  n0,
  output p
);

  wire and_1_out, and_2_out, and_3_out, and_4_out, not_1_out, not_2_out, not_3_out, not_4_out, not_5_out;

  not not_1 (not_1_out, n3);
  and and_1 (and_1_out, not_1_out, n0);
  not not_2 (not_2_out, n3);
  and and_2 (and_2_out, not_2_out, not_3_out, n1);
  not not_3 (not_3_out, n2);
  not not_4 (not_4_out, n2);
  and and_3 (and_3_out, not_4_out, n1, n0);
  and and_4 (and_4_out, n2, not_5_out, n0);
  not not_5 (not_5_out, n1);
  or or_1 (p, and_1_out, and_2_out, and_3_out, and_4_out);
endmodule

module ej4_primo (
  input  enable,
  input  [3:0] in_2,
  output out_3
);

  wire decoder_1_out1, decoder_1_out2, decoder_1_out3, decoder_1_out5, decoder_1_out7, decoder_1_out11,
       decoder_1_out13;

  Decoder #(.select(4)) decoder_1 (
    .out1(decoder_1_out1), .out2(decoder_1_out2), .out3(decoder_1_out3), .out5(decoder_1_out5),
    .out7(decoder_1_out7), .out11(decoder_1_out11), .out13(decoder_1_out13), .sel(in_2), .en(enable));  // open: out0, out4, out6, out8, out9, out10, out12, out14, out15
  or or_1 (out_3, decoder_1_out1, decoder_1_out2, decoder_1_out3, decoder_1_out5, decoder_1_out7, decoder_1_out11, decoder_1_out13);

  // Notes on the sheet:
  //   enable: pull=up
endmodule
