// Logisim project ej5.circ as structural Verilog: 3 circuits, main circuit main
module main (
  input  [4:0] in_1,
  output out_2
);

  ej5_multiplex ej5_multiplex_1 (.in_1(in_1), .lampara(out_2));
endmodule

module ej5_multiplex (
  input  [4:0] in_1,
  output lampara
);

  wire multiplexer_1_out, multiplexer_2_out;

  Multiplexer #(.select(4)) multiplexer_1 (
    .in0(1'b0), .in1(1'b0), .in2(1'b0), .in3(1'b0), .in4(1'b0), .in5(1'b0), .in6(1'b0), .in7(1'b0),
    .in8(1'b0), .in9(1'b1), .in10(1'b0), .in11(1'b1), .in12(1'b0), .in13(1'b1), .in14(1'b1), .in15(1'b1),
    .out(multiplexer_1_out), .sel(in_1[3:0]), .en(1'b1));
  Multiplexer #(.select(4)) multiplexer_2 (
    .in0(1'b0), .in1(1'b0), .in2(1'b0), .in3(1'b1), .in4(1'b0), .in5(1'b1), .in6(1'b0), .in7(1'b1),
    .in8(1'b1), .in9(1'b1), .in10(1'b1), .in11(1'b1), .in12(1'b1), .in13(1'b1), .in14(1'b1), .in15(1'b1),
    .out(multiplexer_2_out), .sel(in_1[3:0]), .en(1'b1));
  mux1 mux1_1 (.D0(multiplexer_1_out), .D1(multiplexer_2_out), .S(in_1[4]), .F(lampara));
endmodule

module mux1 (
  input  D0,
  input  D1,
  input  S,
  output F
);

  wire and_1_out, and_2_out, not_1_out;

  not not_1 (not_1_out, S);
  and and_1 (and_1_out, D1, S);
  and and_2 (and_2_out, D0, not_1_out);
  or or_1 (F, and_1_out, and_2_out);
endmodule
