// Logisim project ejercicio1.circ as structural Verilog: 1 circuit, main circuit main
module main (
  input  [3:0] A,
  input  [3:0] B,
  output [3:0] Sal
);

  wire adder_1_cout, and_1_out, and_2_out, or_1_out;
  wire [2:2] or_2_out;
  wire [3:0] adder_1_out;

  Hex_Digit_Display hex_digit_display_1 (.value(A));  // open: dp
  Hex_Digit_Display hex_digit_display_2 (.value(B));  // open: dp
  Hex_Digit_Display hex_digit_display_3 (.value(adder_1_out));  // open: dp
  Adder #(.width(4)) adder_1 (.a(A), .b(B), .out(adder_1_out), .cin(1'b0), .cout(adder_1_cout));
  and and_1 (and_1_out, adder_1_out[1], adder_1_out[3]);
  and and_2 (and_2_out, adder_1_out[2], adder_1_out[3]);
  Adder #(.width(4)) adder_2 (.a({1'b0, {2{or_2_out[2]}}, 1'b0}), .b(adder_1_out), .out(Sal));  // open: cin, cout
  or or_1 (or_1_out, and_1_out, and_2_out);
  or or_2 (or_2_out[2], or_1_out, adder_1_cout);
  Hex_Digit_Display hex_digit_display_4 (.value({3'b000, or_2_out[2]}));  // open: dp
  Hex_Digit_Display hex_digit_display_5 (.value(Sal));  // open: dp
endmodule
