// Logisim project prac3 5 4.circ as structural Verilog: 4 circuits, main circuit main
module main (
  input  [3:0] A,
  input  [1:0] B,
  input  [3:0] in_3,
  output out_4,
  output out_5,
  output [5:0] P5P4P3P2P1P0
);

  wire [2:0] A1_B0_out;
  wire [3:0] A0_B1_out;

  LedV ledv_1 (.t3(in_3[3]), .t2(in_3[2]), .t1(in_3[1]), .t0(in_3[0]), .LV(out_4));
  LedR ledr_1 (.t3(in_3[3]), .t2(in_3[2]), .t1(in_3[1]), .t0(in_3[0]), .LR(out_5));
  and A3_B1 (A0_B1_out[3], A[0], B[1]);
  Adder #(.width(4)) adder_1 (
    .a({1'b0, A1_B0_out}), .b(A0_B1_out), .out(P5P4P3P2P1P0[4:1]), .cout(P5P4P3P2P1P0[5]));  // open: cin
  and A3_B0 (A1_B0_out[2], A[0], B[0]);
  and A2_B0 (A1_B0_out[1], A[1], B[0]);
  and A2_B1 (A0_B1_out[2], A[1], B[1]);
  and A1_B1 (A0_B1_out[1], A[2], B[1]);
  and A1_B0 (A1_B0_out[0], A[2], B[0]);
  and A0_B0 (P5P4P3P2P1P0[0], A[3], B[0]);
  and A0_B1 (A0_B1_out[0], A[3], B[1]);
endmodule

// LV
module LedV (
  input  t3,
  input  t2,
  input  t1,
  input  t0,
  output LV
);

  wire and_1_out, and_2_out, and_3_out, and_4_out, not_1_out, not_2_out, not_3_out, not_4_out, not_5_out;

  not not_1 (not_1_out, t3);
  not not_2 (not_2_out, t2);
  not not_3 (not_3_out, t3);
  not not_4 (not_4_out, t1);
  not not_5 (not_5_out, t0);
  and and_1 (and_1_out, not_1_out, not_2_out);
  and and_2 (and_2_out, not_3_out, not_4_out, not_5_out);
  and and_3 (and_3_out, t3, t2, t0);
  and and_4 (and_4_out, t3, t2, t1);
  or or_1 (LV, and_1_out, and_2_out, and_3_out, and_4_out);
endmodule

// LR
module LedR (
  input  t3,
  input  t2,
  input  t1,
  input  t0,
  output LR
);

  wire and_1_out, and_2_out, and_3_out, not_1_out, not_2_out, not_3_out, not_4_out, not_5_out;

  not not_1 (not_1_out, t3);
  not not_2 (not_2_out, t2);
  not not_3 (not_3_out, t1);
  not not_4 (not_4_out, t2);
  not not_5 (not_5_out, t0);
  and and_1 (and_1_out, not_1_out, t2, t1);
  and and_2 (and_2_out, t3, not_2_out, not_3_out);
  and and_3 (and_3_out, t3, not_4_out, not_5_out);
  or or_1 (LR, and_1_out, and_2_out, and_3_out);
endmodule

module VotitosNazis (
  input  e,
  input  a,
  input  b,
  input  c,
  input  d
);

  wire multiplexer_1_out;

  Multiplexer #(.select(4)) multiplexer_1 (
    .in0(1'b0), .in1(e), .in2(1'b0), .in3(e), .in4(1'b0), .in5(e), .in6(1'b0), .in7(e), .in8(1'b0),
    .in9(1'b1), .in10(e), .in11(1'b1), .in12(e), .in13(1'b1), .in14(e), .in15(1'b1), .out(multiplexer_1_out),
    .sel({a, b, c, d}));  // open: en
  LED led_1 (.in(multiplexer_1_out));
endmodule
