// Logisim project practica3.circ as structural Verilog
module main (
  input  [3:0] in_1,
  input  [3:0] in_2,
  input  [3:0] in_3
);

  wire adder_1_cout, and_1_out, and_2_out, or_2_out;
  wire [2:2] or_1_out;
  wire [3:0] adder_1_out, adder_2_out;

  Hex_Digit_Display hex_digit_display_1 (.value(in_1));  // open: dp
  Hex_Digit_Display hex_digit_display_2 (.value(in_3));  // open: dp
  Adder #(.width(4)) adder_1 (.a(in_1), .b(in_3), .out(adder_1_out), .cin(1'b0), .cout(adder_1_cout));
  Hex_Digit_Display hex_digit_display_3 (.value(adder_1_out));  // open: dp
  Adder #(.width(4)) adder_2 (
    .a({1'b0, {2{or_1_out[2]}}, 1'b0}), .b(adder_1_out), .out(adder_2_out));  // open: cin, cout
  and and_1 (and_1_out, adder_1_out[1], adder_1_out[3]);
  and and_2 (and_2_out, adder_1_out[2], adder_1_out[3]);
  or or_1 (or_1_out[2], or_2_out, adder_1_cout);
  or or_2 (or_2_out, and_1_out, and_2_out);
  Hex_Digit_Display hex_digit_display_4 (.value({3'b000, or_1_out[2]}));  // open: dp
  Hex_Digit_Display hex_digit_display_5 (.value(adder_2_out));  // open: dp
endmodule

module ej3 (
  input  [3:0] in_1,
  input  [1:0] in_2,
  output [5:0] out_3
);

  wire [2:0] A1_B0_out;
  wire [3:0] A0_B1_out;

  and A3_B0 (A1_B0_out[2], in_1[0], in_2[1]);
  Adder #(.width(4)) adder_1 (.a({1'b0, A1_B0_out}), .b(A0_B1_out), .out(out_3[4:1]), .cout(out_3[5]));  // open: cin
  and A3_B1 (A0_B1_out[3], in_1[0], in_2[0]);
  and A2_B0 (A1_B0_out[1], in_1[1], in_2[1]);
  and A1_B0 (A1_B0_out[0], in_1[2], in_2[1]);
  and A2_B1 (A0_B1_out[2], in_1[1], in_2[0]);
  and A0_B0 (out_3[0], in_1[3], in_2[1]);
  and A1_B1 (A0_B1_out[1], in_1[2], in_2[0]);
  and A0_B1 (A0_B1_out[0], in_1[3], in_2[0]);
endmodule

module ej5 (
  input  a,
  input  b,
  input  c,
  input  d,
  input  e
);
endmodule

module EJ2 (
  input  [3:0] in_1,
  input  [3:0] in_2,
  input  in_3,
  output [3:0] out_4
);

  wire adder_1_cout;
  wire [3:0] xor_1_out;
  wire [3:3] undriven;

  Hex_Digit_Display hex_digit_display_1 (.value(in_1));  // open: dp
  Hex_Digit_Display hex_digit_display_2 (.value(in_2));  // open: dp
  assign xor_1_out = in_2 ^ {{3{undriven[3]}}, in_3};  // XOR_Gate xor_1, 4 bits wide
  Adder #(.width(4)) adder_1 (.a(in_1), .b(xor_1_out), .out(out_4), .cin(undriven[3]), .cout(adder_1_cout));
  Hex_Digit_Display hex_digit_display_3 (.value(out_4));  // open: dp
  // also tied to GND on the sheet: adder_1_cout
endmodule
